# Fritzing sketch RX_stuff (saved by Fritzing 0.9.2b)
breadboards: 1

parts:
  Componente1 = Arduino Micro (Rev3)  # not connected
  NRF24L1 = NRF24L01  # not connected
  LED1 = smd LED [color="Red (633nm)" package="1206 [SMD]"]
  LED2 = smd LED [color="Yellow (595nm)" package="1206 [SMD]"]
  LED3 = smd LED [color="Green (555nm)" package="1206 [SMD]"]
  R1 = Resistor [tolerance=±5% resistance=220 package=THT]
  R2 = Resistor [tolerance=±5% resistance=220 package=THT]
  R3 = Resistor [tolerance=±5% resistance=220 package=THT]

nets:
  N1: LED1.cathode, R1.Pin_0
  N2: LED2.cathode, R2.Pin_0
  N3: LED3.cathode, R3.Pin_0
  N4: R1.Pin_1, R3.Pin_1

custom parts:
  NRF24L01: NRF24L01 module
